# Fritzing sketch CBEfritzingIssue (saved by Fritzing 0.9.3b)
circuit board: 8.46667cm x 5.64444cm
breadboards: 1

parts:
  Q1 = NPN-Transistor [package="TO92 [THT]"]
  R2 = Resistor [tolerance=±5% resistance=2.2k package="0603 [SMD]"]
  VCC1 = Battery
  R1 = Resistor [tolerance=±5% resistance=220 package=THT]
  Raspberry_Pi_1 = Raspberry Pi 3 [part_number=RPI-3-V1.2]  # not connected
  JP1 = USB_MICROB_PLUG [package=micro-b-smt]  # not connected

nets:
  N1: Q1.E, VCC1.-
  N2: Q1.B, R2.Pin_1
  N3: Q1.C, R1.Pin_1
